// Logisim project decode.circ as structural Verilog: 8 circuits, main circuit main
module register_file (
  input  [63:0] writeData,
  input  [3:0] rA,
  input  rAread,
  input  writeEnable,
  input  rBread,
  input  [3:0] writeAddress,
  input  clk,
  input  [3:0] rB,
  output [63:0] valA,
  output [63:0] valB
);

  wire decoder_1_out0, decoder_1_out1, decoder_1_out2, decoder_1_out3, decoder_1_out4, decoder_1_out5,
       decoder_1_out6, decoder_1_out7, decoder_1_out8, decoder_1_out9, decoder_1_out10, decoder_1_out11,
       decoder_1_out12, decoder_1_out13, decoder_1_out14, decoder_1_out15;
  wire [63:0] multiplexer_1_out, multiplexer_2_out, r8_q, r9_q, r10_q, r11_q, r12_q, r13_q, r14_q, r15_q,
       rax_q, rbp_q, rbx_q, rcx_q, rdi_q, rdx_q, rsi_q, rsp_q;

  Decoder #(.select(4)) decoder_1 (
    .out0(decoder_1_out0), .out1(decoder_1_out1), .out2(decoder_1_out2), .out3(decoder_1_out3),
    .out4(decoder_1_out4), .out5(decoder_1_out5), .out6(decoder_1_out6), .out7(decoder_1_out7),
    .out8(decoder_1_out8), .out9(decoder_1_out9), .out10(decoder_1_out10), .out11(decoder_1_out11),
    .out12(decoder_1_out12), .out13(decoder_1_out13), .out14(decoder_1_out14), .out15(decoder_1_out15),
    .sel(writeAddress), .en(writeEnable));
  Register #(.width(64)) rax (.D(writeData), .en(decoder_1_out0), .clk(clk), .Q(rax_q));  // open: clr
  Register #(.width(64)) r15 (.D(writeData), .en(decoder_1_out15), .clk(clk), .Q(r15_q));  // open: clr
  Register #(.width(64)) rcx (.D(writeData), .en(decoder_1_out1), .clk(clk), .Q(rcx_q));  // open: clr
  Register #(.width(64)) r14 (.D(writeData), .en(decoder_1_out14), .clk(clk), .Q(r14_q));  // open: clr
  Register #(.width(64)) rdx (.D(writeData), .en(decoder_1_out2), .clk(clk), .Q(rdx_q));  // open: clr
  Register #(.width(64)) r13 (.D(writeData), .en(decoder_1_out13), .clk(clk), .Q(r13_q));  // open: clr
  Register #(.width(64)) rbx (.D(writeData), .en(decoder_1_out3), .clk(clk), .Q(rbx_q));  // open: clr
  Register #(.width(64)) r12 (.D(writeData), .en(decoder_1_out12), .clk(clk), .Q(r12_q));  // open: clr
  Register #(.width(64)) rsp (.D(writeData), .en(decoder_1_out4), .clk(clk), .Q(rsp_q));  // open: clr
  Register #(.width(64)) r11 (.D(writeData), .en(decoder_1_out11), .clk(clk), .Q(r11_q));  // open: clr
  Register #(.width(64)) rbp (.D(writeData), .en(decoder_1_out5), .clk(clk), .Q(rbp_q));  // open: clr
  Register #(.width(64)) r10 (.D(writeData), .en(decoder_1_out10), .clk(clk), .Q(r10_q));  // open: clr
  Register #(.width(64)) rsi (.D(writeData), .en(decoder_1_out6), .clk(clk), .Q(rsi_q));  // open: clr
  Register #(.width(64)) r9 (.D(writeData), .en(decoder_1_out9), .clk(clk), .Q(r9_q));  // open: clr
  Register #(.width(64)) rdi (.D(writeData), .en(decoder_1_out7), .clk(clk), .Q(rdi_q));  // open: clr
  Register #(.width(64)) r8 (.D(writeData), .en(decoder_1_out8), .clk(clk), .Q(r8_q));  // open: clr
  Multiplexer #(.select(4), .width(64)) multiplexer_1 (
    .in0(rax_q), .in1(rcx_q), .in2(rdx_q), .in3(rbx_q), .in4(rsp_q), .in5(rbp_q), .in6(rsi_q), .in7(rdi_q),
    .in8(r8_q), .in9(r9_q), .in10(r10_q), .in11(r11_q), .in12(r12_q), .in13(r13_q), .in14(r14_q),
    .in15(r15_q), .out(multiplexer_1_out), .sel(rA));
  Multiplexer #(.select(4), .width(64)) multiplexer_2 (
    .in0(rax_q), .in1(rcx_q), .in2(rdx_q), .in3(rbx_q), .in4(rsp_q), .in5(rbp_q), .in6(rsi_q), .in7(rdi_q),
    .in8(r8_q), .in9(r9_q), .in10(r10_q), .in11(r11_q), .in12(r12_q), .in13(r13_q), .in14(r14_q),
    .in15(r15_q), .out(multiplexer_2_out), .sel(rB));
  assign valA = rAread ? multiplexer_1_out : 64'bz;  // Controlled_Buffer controlled_buffer_1
  assign valB = rBread ? multiplexer_2_out : 64'bz;  // Controlled_Buffer controlled_buffer_2

  // Notes on the sheet:
  //   valE or valM
  //   write address
  //   dstE or dstM
  //   read2
  //   read1
endmodule

module main (
  input  [3:0] rB,
  input  [3:0] rA,
  input  [63:0] valM,
  input  [63:0] valE,
  input  in_5,
  input  write_enable,
  input  [3:0] icode,
  input  read_enable,
  output [63:0] valA,
  output [63:0] valB
);

  wire clk_out, ra_logic_1_reada_enable, rb_logic_1_readb_enable;
  wire [3:0] rsp_ra_logic_1_out_3, rsp_rb_logic_1_out_3, write_address_logic_1_write_address;
  wire [63:0] write_data_logic_1_out_4;

  rsp_rB_logic rsp_rb_logic_1 (.rB(rB), .icode(icode), .out_3(rsp_rb_logic_1_out_3));
  rsp_rA_logic rsp_ra_logic_1 (.rA(rA), .icode(icode), .out_3(rsp_ra_logic_1_out_3));
  rA_logic ra_logic_1 (.icode(icode), .read_enable(read_enable), .readA_enable(ra_logic_1_reada_enable));
  rB_logic rb_logic_1 (.icode(icode), .read_enable(read_enable), .readB_enable(rb_logic_1_readb_enable));
  write_address_logic write_address_logic_1 (
    .icode(icode), .cnd(in_5), .rB(rB), .rA(rA), .write_address(write_address_logic_1_write_address));
  Clock clk (.out(clk_out));
  write_data_logic write_data_logic_1 (.icode(icode), .valE(valE), .valM(valM), .out_4(write_data_logic_1_out_4));
  register_file register_file_1 (
    .writeData(write_data_logic_1_out_4), .rA(rsp_ra_logic_1_out_3), .rAread(ra_logic_1_reada_enable),
    .writeEnable(write_enable), .rBread(rb_logic_1_readb_enable),
    .writeAddress(write_address_logic_1_write_address), .clk(clk_out), .rB(rsp_rb_logic_1_out_3),
    .valA(valA), .valB(valB));

  // Notes on the sheet:
  //   for ret, pop, and push we need to use %rsp instead of rA or rB
  //   icode, rA, and rB from fetch
  //   double 
  //   val E or val M
endmodule

module rA_logic (
  input  [3:0] icode,
  input  read_enable,
  output readA_enable
);

  wire call_out, halt_out, irmov_out, jXX_out, mrmov_out, nop_out, nor_1_out;

  and halt (halt_out, ~icode[0], ~icode[1], ~icode[2], ~icode[3]);  // AND_Gate
  and nop (nop_out, icode[0], ~icode[1], ~icode[2], ~icode[3]);  // AND_Gate
  and irmov (irmov_out, icode[0], icode[1], ~icode[2], ~icode[3]);  // AND_Gate
  and jXX (jXX_out, icode[0], icode[1], icode[2], ~icode[3]);  // AND_Gate
  and call (call_out, ~icode[0], ~icode[1], ~icode[2], icode[3]);  // AND_Gate
  and mrmov (mrmov_out, ~icode[0], ~icode[1], icode[2], ~icode[3]);  // AND_Gate
  nor nor_1 (nor_1_out, halt_out, nop_out, irmov_out, jXX_out, call_out, mrmov_out);
  and and_1 (readA_enable, nor_1_out, read_enable);

  // Notes on the sheet:
  //   this is the list of ones that do not read to valA
endmodule

module rB_logic (
  input  [3:0] icode,
  input  read_enable,
  output readB_enable
);

  wire cmov_out, halt_out, irmov_out, jXX_out, nop_out, nor_1_out;

  and halt (halt_out, ~icode[0], ~icode[1], ~icode[2], ~icode[3]);  // AND_Gate
  and nop (nop_out, icode[0], ~icode[1], ~icode[2], ~icode[3]);  // AND_Gate
  and irmov (irmov_out, icode[0], icode[1], ~icode[2], ~icode[3]);  // AND_Gate
  and cmov (cmov_out, ~icode[0], icode[1], ~icode[2], ~icode[3]);  // AND_Gate
  and jXX (jXX_out, icode[0], icode[1], icode[2], ~icode[3]);  // AND_Gate
  nor nor_1 (nor_1_out, nop_out, irmov_out, halt_out, cmov_out, jXX_out);
  and and_1 (readB_enable, nor_1_out, read_enable);
endmodule

module write_address_logic (
  input  [3:0] icode,
  input  cnd,
  input  [3:0] rB,
  input  [3:0] rA,
  output [3:0] write_address
);

  wire call_out, cmov_out, irmov_out, Op_out, push_out, ret_out;
  wire [2:0] or_1_out;

  and cmov (cmov_out, ~icode[0], icode[1], ~icode[2], ~icode[3], cnd);  // AND_Gate
  and irmov (irmov_out, icode[0], icode[1], ~icode[2], ~icode[3]);  // AND_Gate
  and Op (Op_out, ~icode[0], icode[1], icode[2], ~icode[3]);  // AND_Gate
  and mrmov (or_1_out[1], icode[0], ~icode[1], icode[2], ~icode[3]);  // AND_Gate
  and call (call_out, ~icode[0], ~icode[1], ~icode[2], icode[3]);  // AND_Gate
  and ret (ret_out, icode[0], ~icode[1], ~icode[2], icode[3]);  // AND_Gate
  and push (push_out, ~icode[0], icode[1], ~icode[2], icode[3]);  // AND_Gate
  or or_1 (or_1_out[0], cmov_out, irmov_out, Op_out);
  or or_2 (or_1_out[2], call_out, ret_out, push_out);
  Multiplexer #(.select(3), .width(4)) multiplexer_1 (
    .in1(rB), .in2(rA), .in4(4'b0100), .out(write_address), .sel(or_1_out));  // open: in0, in3, in5, in6, in7

  // Notes on the sheet:
  //   writes back to just rA
  //   for functions with multiple wite operations we must provide one address, and wait to provide the second
  //   writes back to just rB
  //   write back to just rsp
  //   use mux to determine address. either rA, rB, or rsp
  //   001: rB
  //   010: rA
  //   100: rsp
endmodule

module rsp_rB_logic (
  input  [3:0] rB,
  input  [3:0] icode,
  output [3:0] out_3
);

  wire call_out, or_1_out, pop_out, push_out, ret_out;

  and call (call_out, ~icode[0], ~icode[1], ~icode[2], icode[3]);  // AND_Gate
  and ret (ret_out, icode[0], ~icode[1], ~icode[2], icode[3]);  // AND_Gate
  and push (push_out, ~icode[0], icode[1], ~icode[2], icode[3]);  // AND_Gate
  and pop (pop_out, icode[0], icode[1], ~icode[2], icode[3]);  // AND_Gate
  or or_1 (or_1_out, call_out, ret_out, push_out, pop_out);
  Multiplexer #(.width(4)) multiplexer_1 (.in0(rB), .in1(4'b0100), .out(out_3), .sel(or_1_out));
endmodule

module rsp_rA_logic (
  input  [3:0] rA,
  input  [3:0] icode,
  output [3:0] out_3
);

  wire or_1_out, pop_out, ret_out;

  and ret (ret_out, icode[0], ~icode[1], ~icode[2], icode[3]);  // AND_Gate
  and pop (pop_out, icode[0], icode[1], ~icode[2], icode[3]);  // AND_Gate
  or or_1 (or_1_out, ret_out, pop_out);
  Multiplexer #(.width(4)) multiplexer_1 (.in0(rA), .in1(4'b0100), .out(out_3), .sel(or_1_out));
endmodule

module write_data_logic (
  input  [3:0] icode,
  input  [63:0] valE,
  input  [63:0] valM,
  output [63:0] out_4
);

  wire call_out, cmov_out, irmov_out, OP_out, push_out, ret_out;
  wire [1:0] or_1_out;

  and cmov (cmov_out, ~icode[0], icode[1], ~icode[2], ~icode[3]);  // AND_Gate
  and irmov (irmov_out, icode[0], icode[1], ~icode[2], ~icode[3]);  // AND_Gate
  and OP (OP_out, ~icode[0], icode[1], icode[2], ~icode[3]);  // AND_Gate
  and call (call_out, ~icode[0], ~icode[1], ~icode[2], icode[3]);  // AND_Gate
  and ret (ret_out, icode[0], ~icode[1], ~icode[2], icode[3]);  // AND_Gate
  and push (push_out, ~icode[0], icode[1], ~icode[2], icode[3]);  // AND_Gate
  and mrmov (or_1_out[1], icode[0], ~icode[1], icode[2], ~icode[3]);  // AND_Gate
  or or_1 (or_1_out[0], cmov_out, irmov_out, OP_out, call_out, ret_out, push_out);
  Multiplexer #(.select(2), .width(64)) multiplexer_1 (
    .in1(valE), .in2(valM), .out(out_4), .sel(or_1_out));  // open: in0, in3

  // Notes on the sheet:
  //   take valM as inptu
  //   take valE as input
endmodule
