// Logisim project ALU_Final.circ as structural Verilog: 5 circuits, main circuit main
module main (
  input  [3:0] icode,
  input  [3:0] ifun,
  input  [63:0] B,
  input  [63:0] A,
  input  [63:0] C,
  output C_ond,
  output [63:0] ValE
);

  wire and_1_out, and_2_out, clock_1_out, controlled_buffer_1_out, decoder_1_out1, decoder_1_out2,
       decoder_1_out3, nand_1_out, O_F_q, or_1_out, SetCC_out, SF_q, xnor_1_out, xor_1_out, ZF_q;
  wire [1:0] encoder_1_s_0, multiplexer_5_out, S_0_out;
  wire [3:2] multiplexer_5_out_2;
  wire [7:0] multiplexer_1_out, multiplexer_1_out_2, multiplexer_1_out_3, multiplexer_1_out_4,
       multiplexer_1_out_5, multiplexer_1_out_6, multiplexer_1_out_7, multiplexer_1_out_8, multiplexer_4_out,
       multiplexer_4_out_2, multiplexer_4_out_3, multiplexer_4_out_4, multiplexer_4_out_5,
       multiplexer_4_out_6, multiplexer_4_out_7, multiplexer_4_out_8;
  wire [63:0] adder_1_out, adder_2_out, and_3_out, multiplexer_2_out, not_1_out, xor_2_out;

  Cond cond_1 (.ZF(ZF_q), .SF(SF_q), .O_F(O_F_q), .Fun(ifun), .out_5(C_ond));
  Clock clock_1 (.out(clock_1_out));
  Register #(.width(1)) ZF (.D(and_1_out), .en(SetCC_out), .clk(clock_1_out), .Q(ZF_q));  // open: clr
  Register #(.width(1)) SF (.D(ValE[63]), .en(SetCC_out), .clk(clock_1_out), .Q(SF_q));  // open: clr
  Register #(.width(1)) O_F (.D(and_2_out), .en(SetCC_out), .clk(clock_1_out), .Q(O_F_q));  // open: clr
  and and_1 (and_1_out, ~ValE[0], ~ValE[1], ~ValE[2], ~ValE[3], ~ValE[4], ~ValE[5], ~ValE[6], ~ValE[7], ~ValE[8], ~ValE[9], ~ValE[10], ~ValE[11], ~ValE[12], ~ValE[13], ~ValE[14], ~ValE[15], ~ValE[16], ~ValE[17], ~ValE[18], ~ValE[19], ~ValE[20], ~ValE[21], ~ValE[22], ~ValE[23], ~ValE[24], ~ValE[25], ~ValE[26], ~ValE[27], ~ValE[28], ~ValE[29], ~ValE[30], ~ValE[31], ~ValE[32], ~ValE[33], ~ValE[34], ~ValE[35], ~ValE[36], ~ValE[37], ~ValE[38], ~ValE[39], ~ValE[40], ~ValE[41], ~ValE[42], ~ValE[43], ~ValE[44], ~ValE[45], ~ValE[46], ~ValE[47], ~ValE[48], ~ValE[49], ~ValE[50], ~ValE[51], ~ValE[52], ~ValE[53], ~ValE[54], ~ValE[55], ~ValE[56], ~ValE[57], ~ValE[58], ~ValE[59], ~ValE[60], ~ValE[61], ~ValE[62], ~ValE[63]);  // AND_Gate
  and and_2 (and_2_out, xor_1_out, xnor_1_out);
  xor xor_1 (xor_1_out, ValE[63], multiplexer_4_out_8[7]);
  xnor xnor_1 (xnor_1_out, multiplexer_4_out_8[7], multiplexer_1_out_8[7]);
  and SetCC (SetCC_out, ~icode[3], icode[2], icode[1], ~icode[0]);  // AND_Gate
  Multiplexer #(.width(64)) multiplexer_1 (
    .in0(multiplexer_2_out), .in1(not_1_out),
    .out({multiplexer_1_out_8, multiplexer_1_out_7, multiplexer_1_out_6, multiplexer_1_out_5, multiplexer_1_out_4, multiplexer_1_out_3, multiplexer_1_out_2, multiplexer_1_out}),
    .sel(decoder_1_out1));
  Multiplexer #(.select(2), .width(64)) multiplexer_2 (
    .in0(A), .in1(C), .in2(64'h8), .in3(64'hfffffffffffffff8), .out(multiplexer_2_out), .sel(encoder_1_s_0));
  assign not_1_out = ~multiplexer_2_out;  // NOT_Gate not_1, 64 bits wide
  encoder encoder_1 (
    .Zero(icode[0]), .One(icode[1]), .Two(icode[2]), .Three(icode[3]), .S_0(encoder_1_s_0[0]),
    .S_1(encoder_1_s_0[1]));
  Adder #(.width(64)) adder_1 (
    .a({multiplexer_4_out_8, multiplexer_4_out_7, multiplexer_4_out_6, multiplexer_4_out_5, multiplexer_4_out_4, multiplexer_4_out_3, multiplexer_4_out_2, multiplexer_4_out}),
    .b(multiplexer_2_out), .out(adder_1_out));  // open: cin, cout
  Adder #(.width(64)) adder_2 (
    .a({multiplexer_4_out_8, multiplexer_4_out_7, multiplexer_4_out_6, multiplexer_4_out_5, multiplexer_4_out_4, multiplexer_4_out_3, multiplexer_4_out_2, multiplexer_4_out}),
    .b(not_1_out), .out(adder_2_out), .cin(1'b1));  // open: cout
  Multiplexer #(.select(2), .width(64)) multiplexer_3 (
    .in0(adder_1_out), .in1(adder_2_out), .in2(and_3_out), .in3(xor_2_out), .out(ValE), .sel(S_0_out));
  assign and_3_out = {multiplexer_4_out_8, multiplexer_4_out_7, multiplexer_4_out_6, multiplexer_4_out_5, multiplexer_4_out_4, multiplexer_4_out_3, multiplexer_4_out_2, multiplexer_4_out} & multiplexer_2_out;  // AND_Gate and_3, 64 bits wide
  assign xor_2_out = {multiplexer_4_out_8, multiplexer_4_out_7, multiplexer_4_out_6, multiplexer_4_out_5, multiplexer_4_out_4, multiplexer_4_out_3, multiplexer_4_out_2, multiplexer_4_out} ^ multiplexer_2_out;  // XOR_Gate xor_2, 64 bits wide
  Multiplexer #(.width(64)) multiplexer_4 (
    .in0({64{1'b0}}), .in1(B),
    .out({multiplexer_4_out_8, multiplexer_4_out_7, multiplexer_4_out_6, multiplexer_4_out_5, multiplexer_4_out_4, multiplexer_4_out_3, multiplexer_4_out_2, multiplexer_4_out}),
    .sel(controlled_buffer_1_out));
  nand nand_1 (nand_1_out, icode[0], icode[1], icode[2], ~icode[3]);  // NAND_Gate
  assign controlled_buffer_1_out = nand_1_out ? or_1_out : 1'bz;  // Controlled_Buffer controlled_buffer_1
  or or_1 (or_1_out, icode[2], icode[3]);
  or S_0 (S_0_out[0], decoder_1_out1, decoder_1_out3);
  or S_1 (S_0_out[1], decoder_1_out2, decoder_1_out3);
  Decoder #(.enable("false"), .select(2)) decoder_1 (
    .out1(decoder_1_out1), .out2(decoder_1_out2), .out3(decoder_1_out3), .sel(multiplexer_5_out));  // open: out0
  Multiplexer #(.width(4)) multiplexer_5 (
    .in0(4'b0000), .in1(ifun), .out({multiplexer_5_out_2, multiplexer_5_out}), .sel(SetCC_out));

  // Notes on the sheet:
  //   CC
  //   ALU A
  //   need to change from 8 bits to 64 changes
  //   ALU B
  //   ALU fun
endmodule

module encoder (
  input  Zero,
  input  One,
  input  Two,
  input  Three,
  output S_0,
  output S_1
);

  wire A_1_out, A_out, C_1_out, C_2_out, C_out, Eight_out, N8_1_out, N8_out, nand_1_out, NEight_out, S0_out,
       S1_out, T8_1_out, T8_out, ValC_out;

  assign S_0 = nand_1_out ? S0_out : 1'bz;  // Controlled_Buffer controlled_buffer_1
  assign S_1 = nand_1_out ? S1_out : 1'bz;  // Controlled_Buffer controlled_buffer_2
  or S0 (S0_out, ValC_out, NEight_out);
  or S1 (S1_out, Eight_out, NEight_out);
  // OR_Gate ValA has open pins: in0=A_out, in1=A_1_out, out=open
  or ValC (ValC_out, C_out, C_1_out, C_2_out);
  or Eight (Eight_out, T8_out, T8_1_out);
  or NEight (NEight_out, N8_out, N8_1_out);
  nand nand_1 (nand_1_out, Zero, One, Two, ~Three);  // NAND_Gate
  and A (A_out, ~Zero, One, ~Two, ~Three);  // AND_Gate
  and C (C_out, Zero, One, ~Two, ~Three);  // AND_Gate
  and C_1 (C_1_out, ~Zero, ~One, Two, ~Three);  // AND_Gate
  and C_2 (C_2_out, Zero, ~One, Two, ~Three);  // AND_Gate
  and A_1 (A_1_out, ~Zero, One, Two, ~Three);  // AND_Gate
  and N8 (N8_out, ~Zero, ~One, ~Two, Three);  // AND_Gate
  and T8 (T8_out, Zero, ~One, ~Two, Three);  // AND_Gate
  and N8_1 (N8_1_out, ~Zero, One, ~Two, Three);  // AND_Gate
  and T8_1 (T8_1_out, Zero, One, ~Two, Three);  // AND_Gate
endmodule

module A_ND (
  input  [63:0] B,
  input  [63:0] A,
  output C,
  output O,
  output T,
  output Th,
  output F,
  output Fi,
  output S,
  output Se
);

  // AND_Gate and_1 has open pins: out=C
  // AND_Gate and_2 has open pins: out=O
  // AND_Gate and_3 has open pins: out=T
  // AND_Gate and_4 has open pins: out=Th
  // AND_Gate and_5 has open pins: out=F
  // AND_Gate and_6 has open pins: out=Fi
  // AND_Gate and_7 has open pins: out=S
  // AND_Gate and_8 has open pins: out=Se
endmodule

module X_OR (
  input  [7:0] B,
  input  [7:0] A,
  output C,
  output O,
  output T,
  output Th,
  output F,
  output Fi,
  output S,
  output Se
);

  xor xor_1 (C, B[0], A[0]);
  xor xor_2 (O, B[1], A[1]);
  xor xor_3 (T, B[2], A[2]);
  xor xor_4 (Th, B[3], A[3]);
  xor xor_5 (F, B[4], A[4]);
  xor xor_6 (Fi, B[5], A[5]);
  xor xor_7 (S, B[6], A[6]);
  xor xor_8 (Se, B[7], A[7]);
endmodule

module Cond (
  input  ZF,
  input  SF,
  input  O_F,
  input  [3:0] Fun,
  output out_5
);

  wire and_1_out, and_2_out, and_3_out, and_4_out, e_out, g_out, ge_out, l_out, le_out, ne_out, or_1_out,
       xor_1_out, xor_2_out;

  and and_1 (and_1_out, ~Fun[3], ~Fun[2], ~Fun[1], ~Fun[0]);  // AND_Gate
  and le (le_out, ~Fun[3], ~Fun[2], ~Fun[1], Fun[0], or_1_out);  // AND_Gate
  or or_1 (or_1_out, ZF, xor_1_out);
  xor xor_1 (xor_1_out, SF, O_F);
  and l (l_out, ~Fun[3], ~Fun[2], Fun[1], ~Fun[0], xor_2_out);  // AND_Gate
  xor xor_2 (xor_2_out, SF, O_F);
  or or_2 (out_5, le_out, l_out, e_out, and_1_out, ne_out, ge_out, g_out);
  and e (e_out, ~Fun[3], ~Fun[2], Fun[1], Fun[0], ZF);  // AND_Gate
  and ne (ne_out, ~Fun[3], Fun[2], ~Fun[1], ~Fun[0], ~ZF);  // AND_Gate
  and ge (ge_out, ~Fun[3], Fun[2], ~Fun[1], Fun[0], and_2_out);  // AND_Gate
  and and_2 (and_2_out, ZF, SF);
  and g (g_out, ~Fun[3], Fun[2], Fun[1], ~Fun[0], and_3_out);  // AND_Gate
  and and_3 (and_3_out, ~ZF, and_4_out);  // AND_Gate
  and and_4 (and_4_out, SF, O_F);
endmodule
