// Logisim project Update_PC.circ as structural Verilog: 1 circuit, main circuit main
module main (
  input  [3:0] icode,
  input  [63:0] C,
  input  Cnd,
  input  [63:0] M,
  input  [63:0] P,
  output [63:0] out_6
);

  wire decoder_1_out1, decoder_1_out2, decoder_1_out3, decoder_1_out4, decoder_1_out5, decoder_1_out6,
       decoder_1_out7, decoder_1_out8, decoder_1_out9, decoder_1_out10, decoder_1_out11,
       demultiplexer_1_out0, demultiplexer_1_out1;
  wire [1:0] ValP_out;

  Decoder #(.enable("false"), .select(4)) decoder_1 (
    .out1(decoder_1_out1), .out2(decoder_1_out2), .out3(decoder_1_out3), .out4(decoder_1_out4),
    .out5(decoder_1_out5), .out6(decoder_1_out6), .out7(decoder_1_out7), .out8(decoder_1_out8),
    .out9(decoder_1_out9), .out10(decoder_1_out10), .out11(decoder_1_out11), .sel(icode));  // open: out0, out12, out13, out14, out15
  Demultiplexer demultiplexer_1 (
    .out0(demultiplexer_1_out0), .out1(demultiplexer_1_out1), .in(decoder_1_out7), .sel(Cnd));
  or ValP (ValP_out[0], decoder_1_out11, decoder_1_out10, decoder_1_out3, decoder_1_out1, decoder_1_out2, decoder_1_out4, decoder_1_out5, decoder_1_out6, decoder_1_out9, demultiplexer_1_out0);
  or ValC (ValP_out[1], decoder_1_out8, demultiplexer_1_out1, decoder_1_out9);
  Multiplexer #(.select(2), .width(64)) multiplexer_1 (
    .in0({64{1'b0}}), .in1(P), .in2(C), .in3(M), .out(out_6), .sel(ValP_out));

  // Notes on the sheet:
  //   0 = 00
  //   P = 01
  //   C = 10
  //   M = 11
endmodule
