// Logisim project finalProject (3).circ as structural Verilog: 14 circuits, main circuit main
module Fetch (
  input  [11:0] PC_in,
  input  fetch_enable,
  input  clk,
  input  PC_update,
  output [3:0] icode,
  output [3:0] ifun,
  output [3:0] rA,
  output [3:0] rB,
  output [63:0] valC,
  output [11:0] valP,
  output fetch_done,
  output halt
);

  wire b1_out, b2_out, b8_out, b9_out, controlled_buffer_1_out, controlled_buffer_2_out, decoder_1_out0,
       decoder_1_out1, decoder_1_out2, decoder_1_out3, decoder_1_out4, decoder_1_out5, decoder_1_out6,
       decoder_1_out7, decoder_1_out8, decoder_1_out9, decoder_1_out10, decoder_2_out0, decoder_2_out1,
       decoder_2_out2, decoder_2_out3, decoder_2_out4, decoder_2_out5, decoder_2_out6, decoder_2_out7,
       decoder_2_out8, decoder_2_out9, decoder_2_out10, decoder_2_out11, or_1_out, or_2_out;
  wire [3:0] adder_2_out, multiplexer_2_out, register_3_q;
  wire [7:0] register_5_q, register_6_q, register_7_q, register_8_q, register_9_q, register_10_q,
       register_11_q, register_12_q, register_13_q, rom_1_data;
  wire [11:0] adder_1_out, multiplexer_1_out, register_2_q;

  or or_1 (or_1_out, fetch_enable, PC_update);
  assign controlled_buffer_1_out = fetch_enable ? clk : 1'bz;  // Controlled_Buffer controlled_buffer_1
  assign controlled_buffer_2_out = or_1_out ? clk : 1'bz;  // Controlled_Buffer controlled_buffer_2
  Register #(.width(12)) register_1 (.D(register_2_q), .en(fetch_done), .clk(clk), .Q(valP));  // open: clr
  ROM #(.addrWidth(12)) rom_1 (.addr(register_2_q), .data(rom_1_data));
  Adder #(.width(12)) adder_1 (.a(register_2_q), .b({12{1'b0}}), .out(adder_1_out), .cin(1'b1));  // open: cout
  Adder #(.width(4)) adder_2 (.a(register_3_q), .b(4'b0000), .out(adder_2_out), .cin(1'b1));  // open: cout
  Register #(.width(12)) register_2 (
    .D(multiplexer_1_out), .clk(controlled_buffer_2_out), .Q(register_2_q));  // open: en, clr
  Multiplexer #(.width(12)) multiplexer_1 (.in0(adder_1_out), .in1(PC_in), .out(multiplexer_1_out), .sel(PC_update));
  Register #(.width(4)) register_3 (
    .D(multiplexer_2_out), .clk(controlled_buffer_1_out), .Q(register_3_q));  // open: en, clr
  Multiplexer #(.width(4)) multiplexer_2 (.in0(adder_2_out), .in1(4'b0000), .out(multiplexer_2_out), .sel(fetch_done));
  Decoder #(.enable("false"), .select(4)) decoder_1 (
    .out0(decoder_1_out0), .out1(decoder_1_out1), .out2(decoder_1_out2), .out3(decoder_1_out3),
    .out4(decoder_1_out4), .out5(decoder_1_out5), .out6(decoder_1_out6), .out7(decoder_1_out7),
    .out8(decoder_1_out8), .out9(decoder_1_out9), .out10(decoder_1_out10), .sel(register_3_q));  // open: out11, out12, out13, out14, out15
  assign fetch_done = b9_out ? decoder_1_out10 : 1'bz;  // Controlled_Buffer controlled_buffer_3
  assign fetch_done = b1_out ? decoder_1_out1 : 1'bz;  // Controlled_Buffer controlled_buffer_4
  assign fetch_done = b2_out ? decoder_1_out2 : 1'bz;  // Controlled_Buffer controlled_buffer_5
  assign fetch_done = b8_out ? decoder_1_out9 : 1'bz;  // Controlled_Buffer controlled_buffer_6
  or b1 (b1_out, decoder_2_out0, decoder_2_out1, decoder_2_out9);
  or b9 (b9_out, decoder_2_out3, decoder_2_out4, decoder_2_out5);
  or b8 (b8_out, decoder_2_out7, decoder_2_out8);
  or b2 (b2_out, decoder_2_out2, decoder_2_out6, decoder_2_out10, decoder_2_out11);
  or or_2 (or_2_out, b2_out, b9_out);
  Register register_4 (.D(rom_1_data), .clk(decoder_1_out1), .Q({icode, ifun}));  // open: en, clr
  Register register_5 (.D(rom_1_data), .clk(decoder_1_out2), .Q(register_5_q));  // open: en, clr
  Register register_6 (.D(rom_1_data), .clk(decoder_1_out3), .Q(register_6_q));  // open: en, clr
  Register register_7 (.D(rom_1_data), .clk(decoder_1_out4), .Q(register_7_q));  // open: en, clr
  Register register_8 (.D(rom_1_data), .clk(decoder_1_out5), .Q(register_8_q));  // open: en, clr
  Register register_9 (.D(rom_1_data), .clk(decoder_1_out6), .Q(register_9_q));  // open: en, clr
  Register register_10 (.D(rom_1_data), .clk(decoder_1_out7), .Q(register_10_q));  // open: en, clr
  Register register_11 (.D(rom_1_data), .clk(decoder_1_out8), .Q(register_11_q));  // open: en, clr
  Register register_12 (.D(rom_1_data), .clk(decoder_1_out9), .Q(register_12_q));  // open: en, clr
  Register register_13 (.D(rom_1_data), .clk(decoder_1_out10), .Q(register_13_q));  // open: en, clr
  Decoder #(.enable("false"), .select(4)) decoder_2 (
    .out0(decoder_2_out0), .out1(decoder_2_out1), .out2(decoder_2_out2), .out3(decoder_2_out3),
    .out4(decoder_2_out4), .out5(decoder_2_out5), .out6(decoder_2_out6), .out7(decoder_2_out7),
    .out8(decoder_2_out8), .out9(decoder_2_out9), .out10(decoder_2_out10), .out11(decoder_2_out11),
    .sel(icode));  // open: out12, out13, out14, out15
  assign {rA, rB} = or_2_out ? register_5_q : 8'bz;  // Controlled_Buffer controlled_buffer_7
  and and_1 (halt, ~fetch_enable, decoder_2_out0);  // AND_Gate
  assign valC = b8_out ? {register_12_q, register_11_q, register_10_q, register_9_q, register_8_q, register_7_q, register_6_q, register_5_q} : 64'bz;  // Controlled_Buffer controlled_buffer_8
  assign valC = b9_out ? {register_13_q, register_12_q, register_11_q, register_10_q, register_9_q, register_8_q, register_7_q, register_6_q} : 64'bz;  // Controlled_Buffer controlled_buffer_9

  // Notes on the sheet:
  //   7,8 should only load icode,ifun, valC
  //   contents of rom_1 (hex, n*v repeats v):
  //   30 f2 3 7*0 30 fa 87 7*0 30 fb 92 7*0 40 25 8*0 30 f0 a 7*0 50 d5 8*0 61 d0 30 f8 51 7*0 75 51 7*0
  //   60 d0 30 f3 1 7*0 10 61 30 30 f9 73 7*0 76 73 7*0 61 30 75 73 7*0 72 87 7*0 61 30 73 92 7*0 30 fc a5
  //   7*0 70 a5
  //   valP
  //   we need instruction byte, register byte, and then destination
  //   2 adders, incrementer and PC +  incrementer.
  //   0,1,9 should only load icode, ifun
  //   2,6,a,b should only load icode, ifun, rA, rB
  //   3,4,5 should load icode, ifun, rA, rB, and valC
  //   load  __ bytes
  //   icode
  //   ifun
  //   rA
  //   rB
  //   valC
  //   1-8
  //   valC
  //   2-9
endmodule

module main (
  output [3:0] rA,
  output [3:0] rB,
  output [3:0] icode,
  output [3:0] ifun,
  output [11:0] new_PC,
  output [63:0] valE,
  output [63:0] valM,
  output [63:0] valA,
  output [63:0] valB,
  output [63:0] valC,
  output [11:0] valP
);

  wire and_1_out, clock_1_out, decode_1_read_done, decode_1_write_done, decoder_1_out0, decoder_1_out1,
       decoder_1_out2, decoder_1_out3, decoder_1_out4, decoder_1_out5, execute_1_cond_out,
       execute_1_execute_done, fetch_1_fetch_done, fetch_1_halt, memory_1_memory_done, or_1_out, or_2_out;
  wire [2:0] adder_1_out, multiplexer_1_out, register_1_q;

  Clock clock_1 (.out(clock_1_out));
  and and_1 (and_1_out, ~fetch_1_halt, clock_1_out);  // AND_Gate
  Fetch fetch_1 (
    .PC_in(new_PC), .fetch_enable(decoder_1_out0), .clk(and_1_out), .PC_update(decoder_1_out5),
    .icode(icode), .ifun(ifun), .rA(rA), .rB(rB), .valC(valC), .valP(valP), .fetch_done(fetch_1_fetch_done),
    .halt(fetch_1_halt));
  Adder #(.width(3)) adder_1 (.a(register_1_q), .b(3'b000), .out(adder_1_out), .cin(1'b1));  // open: cout
  or or_1 (or_1_out, fetch_1_fetch_done, decode_1_read_done, execute_1_execute_done, memory_1_memory_done, decode_1_write_done);
  Register #(.width(3)) register_1 (
    .D(multiplexer_1_out), .en(or_2_out), .clk(and_1_out), .Q(register_1_q));  // open: clr
  Multiplexer #(.width(3)) multiplexer_1 (
    .in0(adder_1_out), .in1(3'b000), .out(multiplexer_1_out), .sel(decoder_1_out5));
  Decoder #(.enable("false"), .select(3)) decoder_1 (
    .out0(decoder_1_out0), .out1(decoder_1_out1), .out2(decoder_1_out2), .out3(decoder_1_out3),
    .out4(decoder_1_out4), .out5(decoder_1_out5), .sel(register_1_q));  // open: out6, out7
  or or_2 (or_2_out, or_1_out, decoder_1_out5);
  Decode decode_1 (
    .valE(valE), .valM(valM), .rB(rB), .rA(rA), .Cond(execute_1_cond_out), .write_enable(decoder_1_out4),
    .icode(icode), .read_enable(decoder_1_out1), .clk(and_1_out), .valA(valA), .valB(valB),
    .read_done(decode_1_read_done), .write_done(decode_1_write_done));
  Execute execute_1 (
    .execute_enable(decoder_1_out2), .clk(and_1_out), .icode(icode), .ifun(ifun), .B(valB), .A(valA),
    .C(valC), .Cond_out(execute_1_cond_out), .valE(valE), .execute_done(execute_1_execute_done));
  Memory memory_1 (
    .clk(and_1_out), .valE(valE), .memory_enable(decoder_1_out3), .valA(valA), .icode(icode), .valP(valP),
    .valM(valM), .memory_done(memory_1_memory_done));
  PC_update pc_update_1 (
    .icode(icode), .Cnd(execute_1_cond_out), .valC(valC), .valM(valM), .valP(valP), .new_PC(new_PC));

  // Notes on the sheet:
  //   FSM controlling stage
  //   write_enable and writeBack_enable are the same
  //   decode_enable and read_enable are the same
  //   this reset will be PC update
  //   PC_update and write_back should be on the same cycle
  //   so basically PC_update occurs at the same time as WB and then should reset the FSM when write is done
endmodule

module Execute (
  input  execute_enable,
  input  clk,
  input  [3:0] icode,
  input  [3:0] ifun,
  input  [63:0] B,
  input  [63:0] A,
  input  [63:0] C,
  output Cond_out,
  output [63:0] valE,
  output execute_done
);

  wire and_1_out, and_2_out, and_3_out, controlled_buffer_1_out, decoder_1_out1, decoder_1_out2,
       decoder_1_out3, nand_1_out, O_F_q, or_1_out, SetCC_out, SF_q, xnor_1_out, xor_1_out, ZF_q;
  wire [1:0] encoder_1_s_0, multiplexer_5_out, S_0_out;
  wire [3:2] multiplexer_5_out_2;
  wire [7:0] multiplexer_1_out, multiplexer_1_out_2, multiplexer_1_out_3, multiplexer_1_out_4,
       multiplexer_1_out_5, multiplexer_1_out_6, multiplexer_1_out_7, multiplexer_1_out_8, multiplexer_4_out,
       multiplexer_4_out_2, multiplexer_4_out_3, multiplexer_4_out_4, multiplexer_4_out_5,
       multiplexer_4_out_6, multiplexer_4_out_7, multiplexer_4_out_8;
  wire [63:0] adder_1_out, adder_2_out, and_4_out, multiplexer_2_out, multiplexer_3_out, not_1_out, xor_2_out;

  Cond cond_1 (.ZF(ZF_q), .SF(SF_q), .O_F(O_F_q), .Fun(ifun), .out_5(Cond_out));
  Register #(.width(1)) ZF (.D(and_2_out), .en(and_1_out), .clk(clk), .Q(ZF_q));  // open: clr
  Register #(.width(1)) SF (.D(multiplexer_3_out[63]), .en(and_1_out), .clk(clk), .Q(SF_q));  // open: clr
  Register #(.width(1)) O_F (.D(and_3_out), .en(and_1_out), .clk(clk), .Q(O_F_q));  // open: clr
  and and_1 (and_1_out, execute_enable, SetCC_out);
  and and_2 (and_2_out, ~multiplexer_3_out[0], ~multiplexer_3_out[1], ~multiplexer_3_out[2], ~multiplexer_3_out[3], ~multiplexer_3_out[4], ~multiplexer_3_out[5], ~multiplexer_3_out[6], ~multiplexer_3_out[7], ~multiplexer_3_out[8], ~multiplexer_3_out[9], ~multiplexer_3_out[10], ~multiplexer_3_out[11], ~multiplexer_3_out[12], ~multiplexer_3_out[13], ~multiplexer_3_out[14], ~multiplexer_3_out[15], ~multiplexer_3_out[16], ~multiplexer_3_out[17], ~multiplexer_3_out[18], ~multiplexer_3_out[19], ~multiplexer_3_out[20], ~multiplexer_3_out[21], ~multiplexer_3_out[22], ~multiplexer_3_out[23], ~multiplexer_3_out[24], ~multiplexer_3_out[25], ~multiplexer_3_out[26], ~multiplexer_3_out[27], ~multiplexer_3_out[28], ~multiplexer_3_out[29], ~multiplexer_3_out[30], ~multiplexer_3_out[31], ~multiplexer_3_out[32], ~multiplexer_3_out[33], ~multiplexer_3_out[34], ~multiplexer_3_out[35], ~multiplexer_3_out[36], ~multiplexer_3_out[37], ~multiplexer_3_out[38], ~multiplexer_3_out[39], ~multiplexer_3_out[40], ~multiplexer_3_out[41], ~multiplexer_3_out[42], ~multiplexer_3_out[43], ~multiplexer_3_out[44], ~multiplexer_3_out[45], ~multiplexer_3_out[46], ~multiplexer_3_out[47], ~multiplexer_3_out[48], ~multiplexer_3_out[49], ~multiplexer_3_out[50], ~multiplexer_3_out[51], ~multiplexer_3_out[52], ~multiplexer_3_out[53], ~multiplexer_3_out[54], ~multiplexer_3_out[55], ~multiplexer_3_out[56], ~multiplexer_3_out[57], ~multiplexer_3_out[58], ~multiplexer_3_out[59], ~multiplexer_3_out[60], ~multiplexer_3_out[61], ~multiplexer_3_out[62], ~multiplexer_3_out[63]);  // AND_Gate
  and and_3 (and_3_out, xor_1_out, xnor_1_out);
  xor xor_1 (xor_1_out, multiplexer_3_out[63], multiplexer_4_out_8[7]);
  xnor xnor_1 (xnor_1_out, multiplexer_4_out_8[7], multiplexer_1_out_8[7]);
  and SetCC (SetCC_out, ~icode[3], icode[2], icode[1], ~icode[0]);  // AND_Gate
  Multiplexer #(.width(64)) multiplexer_1 (
    .in0(multiplexer_2_out), .in1(not_1_out),
    .out({multiplexer_1_out_8, multiplexer_1_out_7, multiplexer_1_out_6, multiplexer_1_out_5, multiplexer_1_out_4, multiplexer_1_out_3, multiplexer_1_out_2, multiplexer_1_out}),
    .sel(decoder_1_out1));
  Multiplexer #(.select(2), .width(64)) multiplexer_2 (
    .in0(A), .in1(C), .in2(64'h8), .in3(64'hfffffffffffffff8), .out(multiplexer_2_out), .sel(encoder_1_s_0));
  assign not_1_out = ~multiplexer_2_out;  // NOT_Gate not_1, 64 bits wide
  encoder encoder_1 (
    .Zero(icode[0]), .One(icode[1]), .Two(icode[2]), .Three(icode[3]), .S_0(encoder_1_s_0[0]),
    .S_1(encoder_1_s_0[1]));
  Adder #(.width(64)) adder_1 (
    .a({multiplexer_4_out_8, multiplexer_4_out_7, multiplexer_4_out_6, multiplexer_4_out_5, multiplexer_4_out_4, multiplexer_4_out_3, multiplexer_4_out_2, multiplexer_4_out}),
    .b(multiplexer_2_out), .out(adder_1_out));  // open: cin, cout
  Adder #(.width(64)) adder_2 (
    .a({multiplexer_4_out_8, multiplexer_4_out_7, multiplexer_4_out_6, multiplexer_4_out_5, multiplexer_4_out_4, multiplexer_4_out_3, multiplexer_4_out_2, multiplexer_4_out}),
    .b(not_1_out), .out(adder_2_out), .cin(1'b1));  // open: cout
  Multiplexer #(.select(2), .width(64)) multiplexer_3 (
    .in0(adder_1_out), .in1(adder_2_out), .in2(and_4_out), .in3(xor_2_out), .out(multiplexer_3_out),
    .sel(S_0_out));
  Register #(.width(64)) valE_reg (.D(multiplexer_3_out), .en(execute_enable), .clk(clk), .Q(valE));  // open: clr
  assign and_4_out = {multiplexer_4_out_8, multiplexer_4_out_7, multiplexer_4_out_6, multiplexer_4_out_5, multiplexer_4_out_4, multiplexer_4_out_3, multiplexer_4_out_2, multiplexer_4_out} & multiplexer_2_out;  // AND_Gate and_4, 64 bits wide
  assign xor_2_out = {multiplexer_4_out_8, multiplexer_4_out_7, multiplexer_4_out_6, multiplexer_4_out_5, multiplexer_4_out_4, multiplexer_4_out_3, multiplexer_4_out_2, multiplexer_4_out} ^ multiplexer_2_out;  // XOR_Gate xor_2, 64 bits wide
  Multiplexer #(.width(64)) multiplexer_4 (
    .in0({64{1'b0}}), .in1(B),
    .out({multiplexer_4_out_8, multiplexer_4_out_7, multiplexer_4_out_6, multiplexer_4_out_5, multiplexer_4_out_4, multiplexer_4_out_3, multiplexer_4_out_2, multiplexer_4_out}),
    .sel(controlled_buffer_1_out));
  nand nand_1 (nand_1_out, icode[0], icode[1], icode[2], ~icode[3]);  // NAND_Gate
  assign controlled_buffer_1_out = nand_1_out ? or_1_out : 1'bz;  // Controlled_Buffer controlled_buffer_1
  or or_1 (or_1_out, icode[2], icode[3]);
  or S_0 (S_0_out[0], decoder_1_out1, decoder_1_out3);
  or S_1 (S_0_out[1], decoder_1_out2, decoder_1_out3);
  Decoder #(.enable("false"), .select(2)) decoder_1 (
    .out1(decoder_1_out1), .out2(decoder_1_out2), .out3(decoder_1_out3), .sel(multiplexer_5_out));  // open: out0
  Multiplexer #(.width(4)) multiplexer_5 (
    .in0(4'b0000), .in1(ifun), .out({multiplexer_5_out_2, multiplexer_5_out}), .sel(SetCC_out));

  assign execute_done = execute_enable;

  // Notes on the sheet:
  //   CC
  //   ALU A
  //   ALU B
  //   ALU fun
endmodule

module encoder (
  input  Zero,
  input  One,
  input  Two,
  input  Three,
  output S_0,
  output S_1
);

  wire A_1_out, A_out, C_1_out, C_2_out, C_out, Eight_out, N8_1_out, N8_out, nand_1_out, NEight_out, S0_out,
       S1_out, T8_1_out, T8_out, ValC_out;

  assign S_0 = nand_1_out ? S0_out : 1'bz;  // Controlled_Buffer controlled_buffer_1
  assign S_1 = nand_1_out ? S1_out : 1'bz;  // Controlled_Buffer controlled_buffer_2
  or S0 (S0_out, ValC_out, NEight_out);
  or S1 (S1_out, Eight_out, NEight_out);
  // OR_Gate ValA has open pins: in0=A_out, in1=A_1_out, out=open
  or ValC (ValC_out, C_out, C_1_out, C_2_out);
  or Eight (Eight_out, T8_out, T8_1_out);
  or NEight (NEight_out, N8_out, N8_1_out);
  nand nand_1 (nand_1_out, Zero, One, Two, ~Three);  // NAND_Gate
  and A (A_out, ~Zero, One, ~Two, ~Three);  // AND_Gate
  and C (C_out, Zero, One, ~Two, ~Three);  // AND_Gate
  and C_1 (C_1_out, ~Zero, ~One, Two, ~Three);  // AND_Gate
  and C_2 (C_2_out, Zero, ~One, Two, ~Three);  // AND_Gate
  and A_1 (A_1_out, ~Zero, One, Two, ~Three);  // AND_Gate
  and N8 (N8_out, ~Zero, ~One, ~Two, Three);  // AND_Gate
  and T8 (T8_out, Zero, ~One, ~Two, Three);  // AND_Gate
  and N8_1 (N8_1_out, ~Zero, One, ~Two, Three);  // AND_Gate
  and T8_1 (T8_1_out, Zero, One, ~Two, Three);  // AND_Gate
endmodule

module Cond (
  input  ZF,
  input  SF,
  input  O_F,
  input  [3:0] Fun,
  output out_5
);

  wire and_1_out, and_2_out, e_out, g_out, ge_out, l_out, le_out, ne_out, or_1_out, xnor_1_out, xor_1_out,
       xor_2_out;

  and and_1 (and_1_out, ~Fun[3], ~Fun[2], ~Fun[1], ~Fun[0]);  // AND_Gate
  and le (le_out, ~Fun[3], ~Fun[2], ~Fun[1], Fun[0], or_1_out);  // AND_Gate
  or or_1 (or_1_out, ZF, xor_1_out);
  xor xor_1 (xor_1_out, SF, O_F);
  and l (l_out, ~Fun[3], ~Fun[2], Fun[1], ~Fun[0], xor_2_out);  // AND_Gate
  xor xor_2 (xor_2_out, SF, O_F);
  or or_2 (out_5, le_out, l_out, e_out, and_1_out, ne_out, ge_out, g_out);
  and e (e_out, ~Fun[3], ~Fun[2], Fun[1], Fun[0], ZF);  // AND_Gate
  and ne (ne_out, ~Fun[3], Fun[2], ~Fun[1], ~Fun[0], ~ZF);  // AND_Gate
  and ge (ge_out, ~Fun[3], Fun[2], ~Fun[1], Fun[0], xnor_1_out);  // AND_Gate
  xnor xnor_1 (xnor_1_out, O_F, SF);
  and g (g_out, ~Fun[3], Fun[2], Fun[1], ~Fun[0], and_2_out);  // AND_Gate
  and and_2 (and_2_out, xnor_1_out, ~ZF);  // AND_Gate
endmodule

module register_file (
  input  useless,
  input  [63:0] writeData,
  input  writeEnable,
  input  [3:0] rA,
  input  rAread,
  input  rBread,
  input  [3:0] writeAddress,
  input  clk,
  input  [3:0] rB,
  input  jmp_in,
  output write_done_out,
  output [63:0] valA,
  output read_done,
  output [63:0] valB
);

  wire and_1_out, and_2_out, and_3_out, decoder_1_out0, decoder_1_out1, decoder_1_out2, decoder_1_out3,
       decoder_1_out4, decoder_1_out5, decoder_1_out6, decoder_1_out7, decoder_1_out8, decoder_1_out9,
       decoder_1_out10, decoder_1_out11, decoder_1_out12, decoder_1_out13, decoder_1_out14, decoder_1_out15,
       decoder_2_out2;
  wire [1:0] adder_1_out, multiplexer_1_out, register_1_q;
  wire [63:0] multiplexer_2_out, multiplexer_3_out, r8_q, r9_q, r10_q, r11_q, r12_q, r13_q, r14_q, r15_q,
       rax_q, rbp_q, rbx_q, rcx_q, rdi_q, rdx_q, rsi_q, rsp_q;

  and and_1 (and_1_out, writeEnable, ~jmp_in);  // AND_Gate
  Decoder #(.select(4)) decoder_1 (
    .out0(decoder_1_out0), .out1(decoder_1_out1), .out2(decoder_1_out2), .out3(decoder_1_out3),
    .out4(decoder_1_out4), .out5(decoder_1_out5), .out6(decoder_1_out6), .out7(decoder_1_out7),
    .out8(decoder_1_out8), .out9(decoder_1_out9), .out10(decoder_1_out10), .out11(decoder_1_out11),
    .out12(decoder_1_out12), .out13(decoder_1_out13), .out14(decoder_1_out14), .out15(decoder_1_out15),
    .sel(writeAddress), .en(and_1_out));
  Register #(.width(64)) rax (.D(writeData), .en(decoder_1_out0), .clk(clk), .Q(rax_q));  // open: clr
  Register #(.width(64)) r15 (.D(writeData), .en(decoder_1_out15), .clk(clk), .Q(r15_q));  // open: clr
  Register #(.width(64)) rcx (.D(writeData), .en(decoder_1_out1), .clk(clk), .Q(rcx_q));  // open: clr
  Register #(.width(64)) r14 (.D(writeData), .en(decoder_1_out14), .clk(clk), .Q(r14_q));  // open: clr
  Register #(.width(2)) register_1 (.D(multiplexer_1_out), .en(writeEnable), .clk(clk), .Q(register_1_q));  // open: clr
  Multiplexer #(.width(2)) multiplexer_1 (
    .in0(adder_1_out), .in1(2'b00), .out(multiplexer_1_out), .sel(decoder_2_out2));
  Adder #(.width(2)) adder_1 (.a(register_1_q), .b(2'b00), .out(adder_1_out), .cin(1'b1));  // open: cout
  Register #(.width(64)) rdx (.D(writeData), .en(decoder_1_out2), .clk(clk), .Q(rdx_q));  // open: clr
  Register #(.width(64)) r13 (.D(writeData), .en(decoder_1_out13), .clk(clk), .Q(r13_q));  // open: clr
  Decoder #(.enable("false"), .select(2)) decoder_2 (
    .out2(decoder_2_out2), .sel(register_1_q));  // open: out0, out1, out3
  and and_2 (and_2_out, decoder_2_out2, and_1_out);
  and and_3 (and_3_out, jmp_in, writeEnable);
  or or_1 (write_done_out, and_2_out, and_3_out);
  Register #(.width(64)) rbx (.D(writeData), .en(decoder_1_out3), .clk(clk), .Q(rbx_q));  // open: clr
  Register #(.width(64)) r12 (.D(writeData), .en(decoder_1_out12), .clk(clk), .Q(r12_q));  // open: clr
  Register #(.width(64)) rsp (.D(writeData), .en(decoder_1_out4), .clk(clk), .Q(rsp_q));  // open: clr
  Register #(.width(64)) r11 (.D(writeData), .en(decoder_1_out11), .clk(clk), .Q(r11_q));  // open: clr
  Register #(.width(64)) rbp (.D(writeData), .en(decoder_1_out5), .clk(clk), .Q(rbp_q));  // open: clr
  Register #(.width(64)) r10 (.D(writeData), .en(decoder_1_out10), .clk(clk), .Q(r10_q));  // open: clr
  Register #(.width(64)) rsi (.D(writeData), .en(decoder_1_out6), .clk(clk), .Q(rsi_q));  // open: clr
  Register #(.width(64)) r9 (.D(writeData), .en(decoder_1_out9), .clk(clk), .Q(r9_q));  // open: clr
  Register #(.width(64)) rdi (.D(writeData), .en(decoder_1_out7), .clk(clk), .Q(rdi_q));  // open: clr
  Register #(.width(64)) r8 (.D(writeData), .en(decoder_1_out8), .clk(clk), .Q(r8_q));  // open: clr
  Multiplexer #(.select(4), .width(64)) multiplexer_2 (
    .in0(rax_q), .in1(rcx_q), .in2(rdx_q), .in3(rbx_q), .in4(rsp_q), .in5(rbp_q), .in6(rsi_q), .in7(rdi_q),
    .in8(r8_q), .in9(r9_q), .in10(r10_q), .in11(r11_q), .in12(r12_q), .in13(r13_q), .in14(r14_q),
    .in15(r15_q), .out(multiplexer_2_out), .sel(rA));
  Multiplexer #(.select(4), .width(64)) multiplexer_3 (
    .in0(rax_q), .in1(rcx_q), .in2(rdx_q), .in3(rbx_q), .in4(rsp_q), .in5(rbp_q), .in6(rsi_q), .in7(rdi_q),
    .in8(r8_q), .in9(r9_q), .in10(r10_q), .in11(r11_q), .in12(r12_q), .in13(r13_q), .in14(r14_q),
    .in15(r15_q), .out(multiplexer_3_out), .sel(rB));
  assign valA = rAread ? multiplexer_2_out : 64'bz;  // Controlled_Buffer controlled_buffer_1
  assign valB = rBread ? multiplexer_3_out : 64'bz;  // Controlled_Buffer controlled_buffer_2
  or or_2 (read_done, rAread, rBread);

  // Notes on the sheet:
  //   write address
  //   dstE or dstM
  //   read1
  //   read2
endmodule

module Decode (
  input  [63:0] valE,
  input  [63:0] valM,
  input  [3:0] rB,
  input  [3:0] rA,
  input  Cond,
  input  write_enable,
  input  [3:0] icode,
  input  read_enable,
  input  clk,
  output [63:0] valA,
  output [63:0] valB,
  output read_done,
  output write_done
);

  wire ra_logic_1_reada_enable, rb_logic_1_readb_enable, register_file_1_read_done, write_logic_1_jmp_out,
       write_logic_1_write_done;
  wire [1:0] adder_1_out, multiplexer_1_out, register_1_q;
  wire [3:0] rsp_ra_logic_1_out_3, rsp_rb_logic_1_out_3, write_logic_1_write_address;
  wire [63:0] register_file_1_vala, register_file_1_valb, write_logic_1_write_data;

  rsp_rB_logic rsp_rb_logic_1 (.rB(rB), .icode(icode), .out_3(rsp_rb_logic_1_out_3));
  rsp_rA_logic rsp_ra_logic_1 (.rA(rA), .icode(icode), .out_3(rsp_ra_logic_1_out_3));
  rA_logic ra_logic_1 (.icode(icode), .read_enable(read_enable), .readA_enable(ra_logic_1_reada_enable));
  rB_logic rb_logic_1 (.icode(icode), .read_enable(read_enable), .readB_enable(rb_logic_1_readb_enable));
  write_logic write_logic_1 (
    .icode(icode), .cnd(Cond), .rA(rA), .valE(valE), .valM(valM), .rB(rB), .clk(clk),
    .write_enable(write_enable), .write_data(write_logic_1_write_data),
    .write_address(write_logic_1_write_address), .write_done(write_logic_1_write_done),
    .jmp_out(write_logic_1_jmp_out));
  register_file register_file_1 (
    .useless(write_logic_1_write_done), .writeData(write_logic_1_write_data), .writeEnable(write_enable),
    .rA(rsp_ra_logic_1_out_3), .rAread(ra_logic_1_reada_enable), .rBread(rb_logic_1_readb_enable),
    .writeAddress(write_logic_1_write_address), .clk(clk), .rB(rsp_rb_logic_1_out_3),
    .jmp_in(write_logic_1_jmp_out), .write_done_out(write_done), .valA(register_file_1_vala),
    .read_done(register_file_1_read_done), .valB(register_file_1_valb));
  Register #(.width(64)) valA_reg (.D(register_file_1_vala), .en(read_enable), .clk(clk), .Q(valA));  // open: clr
  Register #(.width(64)) valB_reg (.D(register_file_1_valb), .en(read_enable), .clk(clk), .Q(valB));  // open: clr
  Adder #(.width(2)) adder_1 (.a(register_1_q), .b(2'b00), .out(adder_1_out), .cin(1'b1));  // open: cout
  Register #(.width(2)) register_1 (.D(multiplexer_1_out), .en(read_enable), .clk(clk), .Q(register_1_q));  // open: clr
  Multiplexer #(.width(2)) multiplexer_1 (.in0(adder_1_out), .in1(2'b00), .out(multiplexer_1_out), .sel(read_done));
  Decoder #(.enable("false"), .select(2)) decoder_1 (.out2(read_done), .sel(register_1_q));  // open: out0, out1, out3
endmodule

module rA_logic (
  input  [3:0] icode,
  input  read_enable,
  output readA_enable
);

  wire call_out, halt_out, irmov_out, jXX_out, mrmov_out, nop_out, nor_1_out;

  and halt (halt_out, ~icode[0], ~icode[1], ~icode[2], ~icode[3]);  // AND_Gate
  and nop (nop_out, icode[0], ~icode[1], ~icode[2], ~icode[3]);  // AND_Gate
  and irmov (irmov_out, icode[0], icode[1], ~icode[2], ~icode[3]);  // AND_Gate
  and jXX (jXX_out, icode[0], icode[1], icode[2], ~icode[3]);  // AND_Gate
  and call (call_out, ~icode[0], ~icode[1], ~icode[2], icode[3]);  // AND_Gate
  and mrmov (mrmov_out, icode[0], ~icode[1], icode[2], ~icode[3]);  // AND_Gate
  nor nor_1 (nor_1_out, halt_out, nop_out, irmov_out, jXX_out, call_out, mrmov_out);
  and and_1 (readA_enable, nor_1_out, read_enable);

  // Notes on the sheet:
  //   this is the list of ones that do not read to valA
endmodule

module rB_logic (
  input  [3:0] icode,
  input  read_enable,
  output readB_enable
);

  wire cmov_out, halt_out, irmov_out, jXX_out, nop_out, nor_1_out;

  and halt (halt_out, ~icode[0], ~icode[1], ~icode[2], ~icode[3]);  // AND_Gate
  and nop (nop_out, icode[0], ~icode[1], ~icode[2], ~icode[3]);  // AND_Gate
  and irmov (irmov_out, icode[0], icode[1], ~icode[2], ~icode[3]);  // AND_Gate
  and cmov (cmov_out, ~icode[0], icode[1], ~icode[2], ~icode[3]);  // AND_Gate
  and jXX (jXX_out, icode[0], icode[1], icode[2], ~icode[3]);  // AND_Gate
  nor nor_1 (nor_1_out, nop_out, irmov_out, halt_out, cmov_out, jXX_out);
  and and_1 (readB_enable, nor_1_out, read_enable);
endmodule

module write_logic (
  input  [3:0] icode,
  input  cnd,
  input  [3:0] rA,
  input  [63:0] valE,
  input  [63:0] valM,
  input  [3:0] rB,
  input  clk,
  input  write_enable,
  output [63:0] write_data,
  output [3:0] write_address,
  output write_done,
  output jmp_out
);

  wire and_1_out, and_2_out, and_3_out, and_4_out, and_5_out, and_6_out, and_7_out, and_9_out, call_out,
       cmov_out, irmov_out, jmp_out_2, nop_out, not_1_out, not_2_out, Op_out, or_4_out, pop_out, push_out,
       ret_out, rmmovq_out;
  wire [1:0] adder_1_out, decoder_1_out0, multiplexer_1_out, or_6_out, register_1_q;
  wire [2:0] or_1_out;
  wire [3:0] multiplexer_2_out, multiplexer_3_out;
  wire [63:0] multiplexer_4_out, multiplexer_5_out;

  Adder #(.width(2)) adder_1 (.a(register_1_q), .b(2'b00), .out(adder_1_out), .cin(1'b1));  // open: cout
  Register #(.width(2)) register_1 (
    .D(multiplexer_1_out), .en(write_enable), .clk(clk), .Q(register_1_q));  // open: clr
  Multiplexer #(.width(2)) multiplexer_1 (
    .in0(adder_1_out), .in1(2'b00), .out(multiplexer_1_out), .sel(decoder_1_out0[1]));
  and cmov (cmov_out, ~icode[0], icode[1], ~icode[2], ~icode[3], cnd);  // AND_Gate
  and irmov (irmov_out, icode[0], icode[1], ~icode[2], ~icode[3]);  // AND_Gate
  and Op (Op_out, ~icode[0], icode[1], icode[2], ~icode[3]);  // AND_Gate
  and mrmov (or_1_out[1], icode[0], ~icode[1], icode[2], ~icode[3]);  // AND_Gate
  and call (call_out, ~icode[0], ~icode[1], ~icode[2], icode[3]);  // AND_Gate
  and ret (ret_out, icode[0], ~icode[1], ~icode[2], icode[3]);  // AND_Gate
  and push (push_out, ~icode[0], icode[1], ~icode[2], icode[3]);  // AND_Gate
  and pop (pop_out, icode[0], icode[1], ~icode[2], icode[3]);  // AND_Gate
  Decoder #(.enable("false"), .select(2)) decoder_1 (
    .out0(decoder_1_out0[0]), .out1(decoder_1_out0[1]), .sel(register_1_q));  // open: out2, out3
  or or_1 (or_1_out[0], cmov_out, irmov_out, Op_out);
  or or_2 (or_1_out[2], call_out, ret_out, push_out);
  or or_3 (write_done, decoder_1_out0[1], and_1_out);
  or or_4 (or_4_out, or_1_out[0], or_1_out[1], or_1_out[2]);
  and and_1 (and_1_out, ~pop_out, or_4_out);  // AND_Gate
  assign write_address = pop_out ? multiplexer_3_out : 4'bz;  // Controlled_Buffer controlled_buffer_1
  Multiplexer #(.select(3), .width(4)) multiplexer_2 (
    .in1(rB), .in2(rA), .in4(4'b0100), .out(multiplexer_2_out), .sel(or_1_out));  // open: in0, in3, in5, in6, in7
  not not_1 (not_1_out, pop_out);
  assign write_address = not_1_out ? multiplexer_2_out : 4'bz;  // Controlled_Buffer controlled_buffer_2
  Multiplexer #(.select(2), .width(4)) multiplexer_3 (
    .in1(4'b0100), .in2(rA), .out(multiplexer_3_out), .sel(decoder_1_out0));  // open: in0, in3
  and and_2 (and_2_out, ~icode[0], icode[1], ~icode[2], ~icode[3]);  // AND_Gate
  and and_3 (and_3_out, icode[0], icode[1], ~icode[2], ~icode[3]);  // AND_Gate
  and and_4 (and_4_out, ~icode[0], icode[1], icode[2], ~icode[3]);  // AND_Gate
  and and_5 (and_5_out, ~icode[0], ~icode[1], ~icode[2], icode[3]);  // AND_Gate
  and and_6 (and_6_out, icode[0], ~icode[1], ~icode[2], icode[3]);  // AND_Gate
  and and_7 (and_7_out, ~icode[0], icode[1], ~icode[2], icode[3]);  // AND_Gate
  and and_8 (or_6_out[1], icode[0], ~icode[1], icode[2], ~icode[3]);  // AND_Gate
  and and_9 (and_9_out, icode[0], icode[1], ~icode[2], icode[3]);  // AND_Gate
  and jmp (jmp_out_2, icode[0], icode[1], icode[2], ~icode[3]);  // AND_Gate
  and nop (nop_out, icode[0], ~icode[1], ~icode[2], ~icode[3]);  // AND_Gate
  and rmmovq (rmmovq_out, ~icode[0], ~icode[1], icode[2], ~icode[3]);  // AND_Gate
  or or_5 (jmp_out, rmmovq_out, nop_out, jmp_out_2);
  or or_6 (or_6_out[0], and_2_out, and_3_out, and_4_out, and_5_out, and_6_out, and_7_out);
  assign write_data = and_9_out ? multiplexer_4_out : 64'bz;  // Controlled_Buffer controlled_buffer_3
  Multiplexer #(.select(2), .width(64)) multiplexer_4 (
    .in1(valE), .in2(valM), .out(multiplexer_4_out), .sel(decoder_1_out0));  // open: in0, in3
  Multiplexer #(.select(2), .width(64)) multiplexer_5 (
    .in1(valE), .in2(valM), .out(multiplexer_5_out), .sel(or_6_out));  // open: in0, in3
  not not_2 (not_2_out, and_9_out);
  assign write_data = not_2_out ? multiplexer_5_out : 64'bz;  // Controlled_Buffer controlled_buffer_4

  // Notes on the sheet:
  //   the reset signal can also be a write done for pop
  //   writes back to just rA
  //   for functions with multiple wite operations we must provide one address, and wait to provide the second
  //   writes back to just rB
  //   write back to just rsp
  //   use mux to determine address. either rA, rB, or rsp
  //   001: rB
  //   010: rA
  //   100: rsp
  //   take valM as inptu
  //   take valE as input
  //   01 is ValE
  //   10 is Val M
endmodule

module rsp_rB_logic (
  input  [3:0] rB,
  input  [3:0] icode,
  output [3:0] out_3
);

  wire call_out, or_1_out, pop_out, push_out, ret_out;

  and call (call_out, ~icode[0], ~icode[1], ~icode[2], icode[3]);  // AND_Gate
  and ret (ret_out, icode[0], ~icode[1], ~icode[2], icode[3]);  // AND_Gate
  and push (push_out, ~icode[0], icode[1], ~icode[2], icode[3]);  // AND_Gate
  and pop (pop_out, icode[0], icode[1], ~icode[2], icode[3]);  // AND_Gate
  or or_1 (or_1_out, call_out, ret_out, push_out, pop_out);
  Multiplexer #(.width(4)) multiplexer_1 (.in0(rB), .in1(4'b0100), .out(out_3), .sel(or_1_out));
endmodule

module rsp_rA_logic (
  input  [3:0] rA,
  input  [3:0] icode,
  output [3:0] out_3
);

  wire or_1_out, pop_out, ret_out;

  and ret (ret_out, icode[0], ~icode[1], ~icode[2], icode[3]);  // AND_Gate
  and pop (pop_out, icode[0], icode[1], ~icode[2], icode[3]);  // AND_Gate
  or or_1 (or_1_out, ret_out, pop_out);
  Multiplexer #(.width(4)) multiplexer_1 (.in0(rA), .in1(4'b0100), .out(out_3), .sel(or_1_out));
endmodule

module Memory (
  input  clk,
  input  [63:0] valE,
  input  memory_enable,
  input  [63:0] valA,
  input  [3:0] icode,
  input  [11:0] valP,
  output [63:0] valM,
  output memory_done
);

  wire decoder_1_out4, decoder_1_out5, decoder_1_out8, decoder_1_out9, decoder_1_out10, decoder_1_out11,
       decoder_2_out2, not_1_out, or_1_out, or_2_out, or_3_out, or_4_out, or_5_out;
  wire [1:0] adder_1_out, multiplexer_1_out, multiplexer_1_out_2, multiplexer_1_out_3, multiplexer_1_out_4,
       multiplexer_1_out_5, multiplexer_1_out_6, multiplexer_1_out_7, multiplexer_1_out_8,
       multiplexer_1_out_9, multiplexer_1_out_10, multiplexer_1_out_11, multiplexer_1_out_12,
       multiplexer_1_out_13, multiplexer_1_out_14, multiplexer_1_out_15, multiplexer_1_out_16,
       multiplexer_1_out_17, multiplexer_1_out_18, multiplexer_1_out_19, multiplexer_1_out_20,
       multiplexer_1_out_21, multiplexer_1_out_22, multiplexer_1_out_23, multiplexer_1_out_24,
       multiplexer_1_out_25, multiplexer_1_out_26, multiplexer_1_out_27, multiplexer_1_out_28,
       multiplexer_1_out_29, multiplexer_1_out_30, multiplexer_1_out_31, multiplexer_1_out_32,
       multiplexer_3_out, register_2_q, undriven, undriven_2, undriven_3, undriven_4, undriven_5, undriven_6,
       undriven_7, undriven_8, undriven_9, undriven_10, undriven_11, undriven_12, undriven_13, undriven_14,
       undriven_15, undriven_16, undriven_17, undriven_18, undriven_19, undriven_20, undriven_21,
       undriven_22, undriven_23, undriven_24, undriven_25, undriven_26;
  wire [3:0] controlled_buffer_1_out;
  wire [63:0] controlled_buffer_2_out, multiplexer_2_out, ram_1_dout;

  Decoder #(.enable("false"), .select(4)) decoder_1 (
    .out4(decoder_1_out4), .out5(decoder_1_out5), .out8(decoder_1_out8), .out9(decoder_1_out9),
    .out10(decoder_1_out10), .out11(decoder_1_out11), .sel(controlled_buffer_1_out));  // open: out0, out1, out2, out3, out6, out7, out12, out13, out14, out15
  assign controlled_buffer_1_out = memory_enable ? icode : 4'bz;  // Controlled_Buffer controlled_buffer_1
  or or_1 (or_1_out, decoder_1_out5, decoder_1_out9, decoder_1_out11);
  or or_2 (or_2_out, decoder_1_out4, decoder_1_out8, decoder_1_out10);
  not not_1 (not_1_out, or_1_out);
  or or_3 (or_3_out, decoder_1_out9, decoder_1_out11);
  or or_4 (or_4_out, decoder_1_out4, decoder_1_out10);
  Multiplexer #(.width(64)) multiplexer_1 (
    .in0(valE), .in1(valA),
    .out({multiplexer_1_out_32, multiplexer_1_out_31, multiplexer_1_out_30, multiplexer_1_out_29, multiplexer_1_out_28, multiplexer_1_out_27, multiplexer_1_out_26, multiplexer_1_out_25, multiplexer_1_out_24, multiplexer_1_out_23, multiplexer_1_out_22, multiplexer_1_out_21, multiplexer_1_out_20, multiplexer_1_out_19, multiplexer_1_out_18, multiplexer_1_out_17, multiplexer_1_out_16, multiplexer_1_out_15, multiplexer_1_out_14, multiplexer_1_out_13, multiplexer_1_out_12, multiplexer_1_out_11, multiplexer_1_out_10, multiplexer_1_out_9, multiplexer_1_out_8, multiplexer_1_out_7, multiplexer_1_out_6, multiplexer_1_out_5, multiplexer_1_out_4, multiplexer_1_out_3, multiplexer_1_out_2, multiplexer_1_out}),
    .sel(or_3_out));
  RAM #(.addrWidth(12), .dataWidth(64)) ram_1 (
    .addr({multiplexer_1_out_6, multiplexer_1_out_5, multiplexer_1_out_4, multiplexer_1_out_3, multiplexer_1_out_2, multiplexer_1_out}),
    .we(or_2_out), .oe(or_1_out), .clk(clk), .din(controlled_buffer_2_out), .dout(ram_1_dout));
  assign controlled_buffer_2_out = not_1_out ? multiplexer_2_out : 64'bz;  // Controlled_Buffer controlled_buffer_2
  Multiplexer #(.width(64)) multiplexer_2 (
    .in0({undriven_26, undriven_25, undriven_24, undriven_23, undriven_22, undriven_21, undriven_20, undriven_19, undriven_18, undriven_17, undriven_16, undriven_15, undriven_14, undriven_13, undriven_12, undriven_11, undriven_10, undriven_9, undriven_8, undriven_7, undriven_6, undriven_5, undriven_4, undriven_3, undriven_2, undriven, valP}),
    .in1(valA), .out(multiplexer_2_out), .sel(or_4_out));
  Register #(.width(64)) register_1 (.D(ram_1_dout), .en(memory_enable), .clk(clk), .Q(valM));  // open: clr
  Adder #(.width(2)) adder_1 (.a(register_2_q), .b(2'b00), .out(adder_1_out), .cin(1'b1));  // open: cout
  Register #(.width(2)) register_2 (.D(multiplexer_3_out), .en(or_5_out), .clk(clk), .Q(register_2_q));  // open: clr
  Multiplexer #(.width(2)) multiplexer_3 (
    .in0(adder_1_out), .in1(2'b00), .out(multiplexer_3_out), .sel(decoder_2_out2));
  or or_5 (or_5_out, memory_enable, decoder_2_out2);
  and and_1 (memory_done, memory_enable, decoder_2_out2);
  Decoder #(.enable("false"), .select(2)) decoder_2 (
    .out2(decoder_2_out2), .sel(register_2_q));  // open: out0, out1, out3

  // Notes on the sheet:
  //   read
  //   write
  //   addr
  //   1 cycle to write
  //   takes 2 cycles to read
  //   data
endmodule

module PC_update (
  input  [3:0] icode,
  input  Cnd,
  input  [63:0] valC,
  input  [63:0] valM,
  input  [11:0] valP,
  output [11:0] new_PC
);

  wire decoder_1_out1, decoder_1_out2, decoder_1_out3, decoder_1_out4, decoder_1_out5, decoder_1_out6,
       decoder_1_out7, decoder_1_out8, decoder_1_out9, decoder_1_out10, decoder_1_out11,
       demultiplexer_1_out0, demultiplexer_1_out1;
  wire [1:0] Val_P_out;

  Decoder #(.enable("false"), .select(4)) decoder_1 (
    .out1(decoder_1_out1), .out2(decoder_1_out2), .out3(decoder_1_out3), .out4(decoder_1_out4),
    .out5(decoder_1_out5), .out6(decoder_1_out6), .out7(decoder_1_out7), .out8(decoder_1_out8),
    .out9(decoder_1_out9), .out10(decoder_1_out10), .out11(decoder_1_out11), .sel(icode));  // open: out0, out12, out13, out14, out15
  Demultiplexer demultiplexer_1 (
    .out0(demultiplexer_1_out0), .out1(demultiplexer_1_out1), .in(decoder_1_out7), .sel(Cnd));
  or Val_P (Val_P_out[0], decoder_1_out11, decoder_1_out10, decoder_1_out3, decoder_1_out1, decoder_1_out2, decoder_1_out4, decoder_1_out5, decoder_1_out6, decoder_1_out9, demultiplexer_1_out0);
  or Val_C (Val_P_out[1], decoder_1_out8, demultiplexer_1_out1, decoder_1_out9);
  Multiplexer #(.select(2), .width(12)) multiplexer_1 (
    .in0({12{1'b0}}), .in1(valP), .in2(valC[11:0]), .in3(valM[11:0]), .out(new_PC), .sel(Val_P_out));

  // Notes on the sheet:
  //   0 = 00
  //   P = 01
  //   C = 10
  //   M = 11
endmodule
